# Fritzing sketch SwitchLed (saved by Fritzing 0.9.3b)
circuit board: 8.46667cm x 5.64444cm
perfboards: 1

parts:
  R1 = Resistor [tolerance=±5% resistance=10k package=THT]
  R2 = Resistor [tolerance=±5% resistance=100 package=THT]
  MCU1 = Raspberry Pi Zero
  LED1 = LED - 5mm [color="Red (633nm)" package="5 mm [THT]"]
  S1 = Pushbutton [package="[THT]"]

nets:
  N1: R1.Pin_0, MCU1.pin_37
  N2: R1.Pin_1, MCU1.pin_40, S1.Pin_3, S1.Pin_4
  N3: R2.Pin_0, LED1.anode
  N4: R2.Pin_1, MCU1.pin_38
  N5: MCU1.pin_34, MCU1.pin_39, LED1.cathode, S1.Pin_1, S1.Pin_2
