# Fritzing sketch OttoPi-01 (saved by Fritzing 0.9.3b)
circuit board: 7.84638cm x 6.17067cm
perfboards: 1

parts:
  MCU1 = Raspberry Pi Zero
  J16 = female pin header, 5 pins [form="♀ (female)"]
  J17 = female pin header, 5 pins [form="♀ (female)"]
  LED1 = LED - 5mm [color="Red (633nm)" package="5 mm [THT]"]
  S1 = Pushbutton [package="[THT]"]
  R1 = Resistor [tolerance=±5% resistance=220 package=THT]
  S2 = Toggle Switch [package=THT]
  J18 = female pin header, 7 pins [form="♀ (female)"]
  J19 = female pin header, 7 pins [form="♀ (female)"]
  J7 = female pin header, 3 pins [form="♀ (female)"]
  J8 = female pin header, 3 pins [form="♀ (female)"]
  J9 = female pin header, 3 pins [form="♀ (female)"]
  J3 = female pin header, 3 pins [form="♀ (female)"]
  J4 = female pin header, 3 pins [form="♀ (female)"]
  J5 = female pin header, 3 pins [form="♀ (female)"]
  J6 = female pin header, 3 pins [form="♀ (female)"]
  R2 = Resistor [tolerance=±5% resistance=220 package=THT]
  VCC1 = Battery
  J22 = female pin header, 20 pins [form="♀ (female)"]
  J23 = female pin header, 20 pins [form="♀ (female)"]
  J24 = female pin header, 5 pins [form="♀ (female)"]
  J21 = female pin header, 11 pins [form="♀ (female)"]

nets:
  N1: MCU1.pin_1, MCU1.pin_17, J16.pin1, J17.pin1, J22.pin12, J22.pin20, J24.pin1
  N2: MCU1.pin_2, MCU1.pin_4, J19.pin1, J23.pin19, J23.pin20, J21.pin7
  N3: MCU1.pin_3, J16.pin2, J17.pin2, J22.pin19, J24.pin2
  N4: MCU1.pin_5, J16.pin3, J17.pin3, J22.pin18, J24.pin3
  N5: MCU1.pin_6, MCU1.pin_9, MCU1.pin_14, MCU1.pin_20, MCU1.pin_25, MCU1.pin_30, MCU1.pin_34, MCU1.pin_39, J16.pin5, J17.pin5, LED1.cathode, S1.Pin_1, S1.Pin_2, J7.pin1, J8.pin1, J9.pin1, J3.pin1, J4.pin1, J5.pin1, J6.pin1, VCC1.-, J22.pin1, J22.pin8, J22.pin16, J23.pin4, J23.pin6, J23.pin11, J23.pin14, J23.pin18, J24.pin5, J21.pin6, J21.pin10
  N6: MCU1.pin_7, J16.pin4, J17.pin4, J22.pin17, J24.pin4
  N7: MCU1.pin_8, J23.pin17
  N8: MCU1.pin_10, J23.pin16
  N9: MCU1.pin_11, J22.pin15
  N10: MCU1.pin_12, J23.pin15
  N11: MCU1.pin_13, J22.pin14
  N12: MCU1.pin_15, J22.pin13
  N13: MCU1.pin_16, J23.pin13
  N14: MCU1.pin_18, J23.pin12
  N15: MCU1.pin_19, J22.pin11
  N16: MCU1.pin_21, J22.pin10
  N17: MCU1.pin_22, J23.pin10
  N18: MCU1.pin_23, J22.pin9
  N19: MCU1.pin_24, J23.pin9
  N20: MCU1.pin_26, J23.pin8
  N21: MCU1.pin_27, J22.pin7
  N22: MCU1.pin_28, J23.pin7
  N23: MCU1.pin_29, J22.pin6
  N24: MCU1.pin_31, J22.pin5
  N25: MCU1.pin_32, J23.pin5
  N26: MCU1.pin_33, J22.pin4, J21.pin9
  N27: MCU1.pin_35, J22.pin3
  N28: MCU1.pin_36, J23.pin3
  N29: MCU1.pin_37, R2.Pin_1, J22.pin2
  N30: MCU1.pin_38, R1.Pin_1, J23.pin2
  N31: MCU1.pin_40, S1.Pin_3, S1.Pin_4, R2.Pin_0, J23.pin1
  N32: LED1.anode, R1.Pin_0
  N33: S2.COM, J18.pin1, J7.pin2, J8.pin2, J9.pin2, J3.pin2, J4.pin2, J5.pin2, J6.pin2
  N34: S2.L2, VCC1.+
  N35: J18.pin7, J19.pin7
