# Fritzing sketch OttoPi-02 (saved by Fritzing 0.9.3b)
circuit board: 8cm x 5.5cm
perfboards: 2

parts:
  J3 = female pin header, 3 pins [form="♀ (female)"]
  J26 = female pin header, 2 pins [form="♀ (female)"]
  R1 = Resistor [tolerance=±5% resistance=220 package=THT]
  MCU1 = Raspberry Pi Zero
  J25 = female pin header, 2 pins [form="♀ (female)"]
  J5 = female pin header, 3 pins [form="♀ (female)"]
  R2 = Resistor [tolerance=±5% resistance=10k package=THT]
  S2 = Toggle Switch [package=THT]
  S1 = Pushbutton [package="[THT]"]
  J24 = female pin header, 5 pins [form="♀ (female)"]
  VCC1 = Battery
  J4 = female pin header, 3 pins [form="♀ (female)"]
  J27 = female pin header, 4 pins [form="♀ (female)"]
  LED1 = LED - 5mm [color="Red (633nm)" package="5 mm [THT]"]
  J32 = female pin header, 2 pins [form="♀ (female)"]
  J30 = female pin header, 1 pin [form="♀ (female)"]
  J28 = female pin header, 1 pin [form="♀ (female)"]
  J16 = female pin header, 5 pins [form="♀ (female)"]
  J9 = female pin header, 3 pins [form="♀ (female)"]
  J7 = female pin header, 3 pins [form="♀ (female)"]
  J8 = female pin header, 3 pins [form="♀ (female)"]
  J6 = female pin header, 3 pins [form="♀ (female)"]
  J34 = female pin header, 10 pins [form="♀ (female)"]  # not connected
  J35 = female pin header, 1 pin [form="♀ (female)"]  # not connected
  R4 = Resistor [tolerance=±5% resistance=270 package=THT]
  R5 = Resistor [tolerance=±5% resistance=150 package=THT]
  C1 = Ceramic Capacitor [capacitance=10nF package="100 mil [THT, multilayer]"]
  C2 = Electrolytic Capacitor [capacitance=1µF package="100 mil [THT, electrolytic]"]
  J36 = female pin header, 2 pins [form="♀ (female)"]
  J32_2 = female pin header, 3 pins [form="♀ (female)"]
  J33 = female pin header, 1 pin [form="♀ (female)"]

nets:
  N1: J3.pin1, MCU1.pin_6, MCU1.pin_9, MCU1.pin_14, MCU1.pin_20, MCU1.pin_25, MCU1.pin_30, MCU1.pin_34, MCU1.pin_39, J5.pin1, S1.Pin_1, S1.Pin_2, J24.pin1, VCC1.-, J4.pin1, LED1.cathode, J32.pin1, J28.pin1, J16.pin1, J9.pin1, J7.pin1, J8.pin1, J6.pin1, R5.Pin_1, C1.1, J36.pin1, J32_2.pin2, J33.pin1
  N2: J3.pin2, J5.pin2, S2.COM, J4.pin2, J30.pin1, J9.pin2, J7.pin2, J8.pin2, J6.pin2
  N3: J26.pin1, J27.pin2
  N4: J26.pin2, J27.pin1
  N5: R1.Pin_0, LED1.anode
  N6: R1.Pin_1, MCU1.pin_40
  N7: MCU1.pin_1, MCU1.pin_17, R2.Pin_1, J24.pin5, J16.pin5
  N8: MCU1.pin_2, MCU1.pin_4, J32.pin2
  N9: MCU1.pin_3, J24.pin4, J16.pin4
  N10: MCU1.pin_5, J24.pin3, J16.pin3
  N11: MCU1.pin_7, J24.pin2, J16.pin2
  N12: MCU1.pin_33, R4.Pin_0
  N13: MCU1.pin_38, R2.Pin_0, S1.Pin_3, S1.Pin_4, J36.pin2
  N14: J25.pin1, J27.pin3
  N15: J25.pin2, J27.pin4
  N16: S2.L1, VCC1.+
  N17: R4.Pin_1, R5.Pin_0, C1.0, C2.+
  N18: C2.-, J32_2.pin3
