# Fritzing sketch OttoPi-04 (saved by Fritzing 0.9.3b)
circuit board: 6.6cm x 6.6cm
perfboards: 2

parts:
  M20 = female pin header, 3 pins [form="♀ (female)"]
  R1 = Resistor [tolerance=±5% resistance=220 package=THT]
  SPK = female pin header, 2 pins [form="♀ (female)"]
  M12 = female pin header, 3 pins [form="♀ (female)"]
  R2 = Resistor [tolerance=±5% resistance=10k package=THT]
  PW = Toggle Switch [package=THT]
  S1 = Pushbutton [package="[THT]"]
  I2C1 = female pin header, 5 pins [form="♀ (female)"]
  VCC1 = Battery
  M16 = female pin header, 3 pins [form="♀ (female)"]
  J27 = female pin header, 4 pins [form="♀ (female)"]
  LED19 = LED - 5mm [color="Red (633nm)" package="5 mm [THT]"]
  J30 = female pin header, 1 pin [form="♀ (female)"]
  J28 = female pin header, 1 pin [form="♀ (female)"]
  I2C2 = female pin header, 5 pins [form="♀ (female)"]
  M24 = female pin header, 3 pins [form="♀ (female)"]
  M8 = female pin header, 3 pins [form="♀ (female)"]
  M25 = female pin header, 3 pins [form="♀ (female)"]
  M7 = female pin header, 3 pins [form="♀ (female)"]
  J35 = female pin header, 1 pin [form="♀ (female)"]
  SW26 = female pin header, 2 pins [form="♀ (female)"]
  J32 = female pin header, 3 pins [form="♀ (female)"]
  J33 = female pin header, 1 pin [form="♀ (female)"]
  MCU1 = Raspberry Pi Zero
  J32_2 = female pin header, 2 pins [form="♀ (female)"]
  R3 = Resistor [tolerance=±5% resistance=150 package=THT]
  M23 = female pin header, 3 pins [form="♀ (female)"]
  M18 = female pin header, 3 pins [form="♀ (female)"]
  GND = female pin header, 2 pins [form="♀ (female)"]
  C1 = Ceramic Capacitor [capacitance=100nF voltage=50V package="100 mil [THT, multilayer]"]

nets:
  N1: M20.pin1, M12.pin1, S1.Pin_1, S1.Pin_2, I2C1.pin1, VCC1.-, M16.pin1, LED19.cathode, J28.pin1, I2C2.pin1, M24.pin1, M8.pin1, M25.pin1, M7.pin1, SW26.pin1, J32.pin2, J33.pin1, MCU1.pin_6, MCU1.pin_9, MCU1.pin_20, MCU1.pin_39, J32_2.pin1, M23.pin1, M18.pin1, GND.pin1, C1.1
  N2: M20.pin2, M12.pin2, PW.COM, M16.pin2, J30.pin1, M24.pin2, M8.pin2, M25.pin2, M7.pin2, J32_2.pin2, M23.pin2, M18.pin2
  N3: M20.pin3, MCU1.pin_38
  N4: R1.Pin_0, LED19.anode
  N5: R1.Pin_1, MCU1.pin_35
  N6: SPK.pin1, J27.pin3
  N7: SPK.pin2, J27.pin4
  N8: M12.pin3, MCU1.pin_32
  N9: R2.Pin_0, S1.Pin_3, S1.Pin_4, SW26.pin2, MCU1.pin_40
  N10: R2.Pin_1, MCU1.pin_37
  N11: PW.L1, VCC1.+, GND.pin2
  N12: I2C1.pin2, I2C2.pin2, MCU1.pin_7
  N13: I2C1.pin3, I2C2.pin3, MCU1.pin_5
  N14: I2C1.pin4, I2C2.pin4, MCU1.pin_3
  N15: I2C1.pin5, I2C2.pin5, MCU1.pin_1, MCU1.pin_17
  N16: M16.pin3, MCU1.pin_36
  N17: M24.pin3, MCU1.pin_18
  N18: M8.pin3, MCU1.pin_24
  N19: M25.pin3, MCU1.pin_22
  N20: M7.pin3, MCU1.pin_26
  N21: J35.pin1, MCU1.pin_2
  N22: J32.pin1, R3.Pin_1, C1.0
  N23: MCU1.pin_12, M18.pin3
  N24: MCU1.pin_16, M23.pin3
  N25: MCU1.pin_33, R3.Pin_0
