# Fritzing sketch OttoPi-05a (saved by Fritzing 0.9.3b)
circuit board: 5.5cm x 6.5cm
perfboards: 1

parts:
  VCC1 = Battery
  J1 = female pin header, 3 pins [form="♀ (female)"]
  S1 = Toggle Switch [package=THT]
  J2 = female pin header, 2 pins [form="♀ (female)"]
  J3 = female pin header, 4 pins [form="♀ (female)"]
  J4 = female pin header, 2 pins [form="♀ (female)"]
  J5 = female pin header, 4 pins [form="♀ (female)"]
  J7 = female pin header, 20 pins [form="♀ (female)"]
  J8 = female pin header, 20 pins [form="♀ (female)"]
  J9 = female pin header, 4 pins [form="♀ (female)"]
  C1 = Ceramic Capacitor [capacitance=100nF package="100 mil [THT, multilayer]"]
  J13 = female pin header, 4 pins [form="♀ (female)"]
  J14 = female pin header, 4 pins [form="♀ (female)"]
  J15 = female pin header, 4 pins [form="♀ (female)"]
  J16 = female pin header, 4 pins [form="♀ (female)"]
  J17 = female pin header, 4 pins [form="♀ (female)"]
  J19 = female pin header, 2 pins [form="♀ (female)"]
  MCU1 = Raspberry Pi Zero
  J12 = female pin header, 24 pins [form="♀ (female)"]  # not connected
  J20 = female pin header, 2 pins [form="♀ (female)"]
  J6 = female pin header, 4 pins [form="♀ (female)"]

nets:
  N1: VCC1.-, J1.pin2, J2.pin1, J3.pin1, J3.pin3, J5.pin4, J7.pin3, J7.pin17, J8.pin5, J8.pin13, J8.pin20, J9.pin1, C1.1, J13.pin4, J14.pin4, J15.pin4, J16.pin4, J17.pin4, MCU1.pin_6, MCU1.pin_9, MCU1.pin_25, MCU1.pin_34, MCU1.pin_39, J6.pin4
  N2: VCC1.+, S1.L2, J2.pin2
  N3: J1.pin1, J7.pin1, J7.pin2, MCU1.pin_2, MCU1.pin_4
  N4: J1.pin3, S1.COM, J3.pin4, J5.pin3, J13.pin3, J14.pin3, J15.pin3, J16.pin3, J17.pin3, J6.pin3
  N5: J3.pin2, C1.0, J20.pin2
  N6: J4.pin1, J19.pin1
  N7: J4.pin2, J19.pin2
  N8: J5.pin2, J8.pin4, MCU1.pin_7
  N9: J7.pin4, MCU1.pin_8
  N10: J7.pin5, MCU1.pin_10
  N11: J7.pin16, MCU1.pin_32
  N12: J8.pin1, J8.pin9, J9.pin4, MCU1.pin_1, MCU1.pin_17
  N13: J8.pin2, J9.pin3, MCU1.pin_3
  N14: J8.pin3, J9.pin2, MCU1.pin_5
  N15: J8.pin6, MCU1.pin_11, J6.pin2
  N16: J8.pin7, J13.pin2, MCU1.pin_13
  N17: J8.pin8, J14.pin2, MCU1.pin_15
  N18: J8.pin10, MCU1.pin_19
  N19: J8.pin11, MCU1.pin_21
  N20: J8.pin12, MCU1.pin_23
  N21: J8.pin14, J15.pin2, MCU1.pin_27
  N22: J8.pin15, J16.pin2, MCU1.pin_29
  N23: J8.pin16, J17.pin2, MCU1.pin_31
  N24: J8.pin17, MCU1.pin_33, J20.pin1
