# Fritzing sketch OttoPi-05b (saved by Fritzing 0.9.3b)
circuit board: 5.5cm x 6.5cm
perfboards: 1

parts:
  J1 = female pin header, 3 pins [form="♀ (female)"]
  S1 = Toggle Switch [package=THT]
  J2 = female pin header, 2 pins [form="♀ (female)"]
  AMP = female pin header, 4 pins [form="♀ (female)"]
  AMP_O = female pin header, 2 pins [form="♀ (female)"]
  J5 = female pin header, 4 pins [form="♀ (female)"]
  J7 = female pin header, 20 pins [form="♀ (female)"]
  J8 = female pin header, 20 pins [form="♀ (female)"]
  J9 = female pin header, 4 pins [form="♀ (female)"]
  C1 = Ceramic Capacitor [capacitance=100nF package="100 mil [THT, multilayer]"]
  J13 = female pin header, 4 pins [form="♀ (female)"]
  J14 = female pin header, 4 pins [form="♀ (female)"]
  J15 = female pin header, 4 pins [form="♀ (female)"]
  J16 = female pin header, 4 pins [form="♀ (female)"]
  SP = female pin header, 2 pins [form="♀ (female)"]
  MCU1 = Raspberry Pi Zero
  J12 = female pin header, 24 pins [form="♀ (female)"]  # not connected
  VOL = female pin header, 2 pins [form="♀ (female)"]
  J6 = female pin header, 4 pins [form="♀ (female)"]
  VCC1 = Battery
  R1 = Resistor [tolerance=±5% resistance=220 package=THT]
  LED1 = LED - 5mm [color="Red (633nm)" package="5 mm [THT]"]
  J21 = female pin header, 2 pins [form="♀ (female)"]
  R2 = Resistor [tolerance=±5% resistance=220 package=THT]
  J22 = female pin header, 2 pins [form="♀ (female)"]
  J23 = female pin header, 2 pins [form="♀ (female)"]

nets:
  N1: J1.pin1, J7.pin1, J7.pin2, MCU1.pin_2, MCU1.pin_4
  N2: J1.pin2, J2.pin1, AMP.pin1, AMP.pin3, J5.pin4, J7.pin3, J7.pin7, J7.pin10, J7.pin15, J7.pin17, J8.pin5, J8.pin13, J8.pin20, J9.pin1, C1.1, J13.pin4, J14.pin4, J15.pin4, J16.pin4, MCU1.pin_6, MCU1.pin_9, MCU1.pin_14, MCU1.pin_20, MCU1.pin_25, MCU1.pin_30, MCU1.pin_34, MCU1.pin_39, J6.pin4, VCC1.-, R1.Pin_1, J21.pin2, J22.pin1, J23.pin1
  N3: J1.pin3, S1.COM, AMP.pin4, J5.pin3, J13.pin3, J14.pin3, J15.pin3, J16.pin3, J6.pin3, LED1.anode, J22.pin2, J23.pin2
  N4: S1.L2, J2.pin2, VCC1.+
  N5: AMP.pin2, C1.0, VOL.pin2
  N6: AMP_O.pin1, SP.pin1
  N7: AMP_O.pin2, SP.pin2
  N8: J7.pin4, MCU1.pin_8
  N9: J7.pin5, MCU1.pin_10
  N10: J7.pin6, MCU1.pin_12
  N11: J7.pin8, MCU1.pin_16
  N12: J7.pin9, MCU1.pin_18
  N13: J7.pin11, MCU1.pin_22
  N14: J7.pin12, MCU1.pin_24
  N15: J7.pin13, MCU1.pin_26
  N16: J7.pin14, MCU1.pin_28
  N17: J7.pin16, MCU1.pin_32, VOL.pin1
  N18: J7.pin18, MCU1.pin_36
  N19: J7.pin19, MCU1.pin_38
  N20: J7.pin20, MCU1.pin_40
  N21: J8.pin1, J8.pin9, J9.pin4, MCU1.pin_1, MCU1.pin_17
  N22: J8.pin2, J9.pin3, MCU1.pin_3
  N23: J8.pin3, J9.pin2, MCU1.pin_5
  N24: J8.pin4, MCU1.pin_7, R2.Pin_1
  N25: J8.pin6, MCU1.pin_11, J21.pin1, R2.Pin_0
  N26: J8.pin7, MCU1.pin_13
  N27: J8.pin8, MCU1.pin_15
  N28: J8.pin10, MCU1.pin_19
  N29: J8.pin11, MCU1.pin_21
  N30: J8.pin12, MCU1.pin_23
  N31: J8.pin14, MCU1.pin_27
  N32: J8.pin15, MCU1.pin_29
  N33: J8.pin16, MCU1.pin_31
  N34: J8.pin17, MCU1.pin_33
  N35: J8.pin18, MCU1.pin_35
  N36: J8.pin19, MCU1.pin_37
  N37: R1.Pin_0, LED1.cathode
