# Fritzing sketch OttoPi-05c (saved by Fritzing 0.9.3b)
circuit board: 5.5cm x 6.5cm
perfboards: 1

parts:
  5V = female pin header, 3 pins [form="♀ (female)"]
  POW = Toggle Switch [package=THT]
  AMP = female pin header, 4 pins [form="♀ (female)"]
  J5 = female pin header, 4 pins [form="♀ (female)"]
  I2C2 = female pin header, 4 pins [form="♀ (female)"]
  C1 = Ceramic Capacitor [capacitance=100nF package="100 mil [THT, multilayer]"]
  J13 = female pin header, 4 pins [form="♀ (female)"]
  J14 = female pin header, 4 pins [form="♀ (female)"]
  J15 = female pin header, 4 pins [form="♀ (female)"]
  J16 = female pin header, 4 pins [form="♀ (female)"]
  MCU1 = Raspberry Pi Zero
  J12 = female pin header, 24 pins [form="♀ (female)"]  # not connected
  VOL = female pin header, 2 pins [form="♀ (female)"]
  J6 = female pin header, 4 pins [form="♀ (female)"]
  R2 = Resistor [tolerance=±5% resistance=330 package=THT]
  I2C = female pin header, 4 pins [form="♀ (female)"]
  J23 = female pin header, 4 pins [form="♀ (female)"]
  R3 = Resistor [tolerance=±5% resistance=10k package=THT]
  U1 = LIPO-2000mAh [package=lipo-2000]
  SP+ = female pin header, 1 pin [form="♀ (female)"]
  SP- = female pin header, 1 pin [form="♀ (female)"]
  SP+_2 = female pin header, 1 pin [form="♀ (female)"]
  SP-_2 = female pin header, 1 pin [form="♀ (female)"]
  POW_2 = LED - 5mm [color="Red (633nm)" package="5 mm [THT]"]
  R4 = Resistor [tolerance=±5% resistance=330 package=THT]
  GND = female pin header, 1 pin [form="♀ (female)"]
  VCC = female pin header, 1 pin [form="♀ (female)"]
  GPIO_SW = female pin header, 1 pin [form="♀ (female)"]
  GPIO_LED = female pin header, 1 pin [form="♀ (female)"]
  LED = female pin header, 1 pin [form="♀ (female)"]
  - = female pin header, 1 pin [form="♀ (female)"]
  SW = female pin header, 2 pins [form="♀ (female)"]
  VOUT = female pin header, 2 pins [form="♀ (female)"]
  GPIO_IN = female pin header, 1 pin [form="♀ (female)"]
  3V = female pin header, 1 pin [form="♀ (female)"]
  I = female pin header, 1 pin [form="♀ (female)"]
  G = female pin header, 1 pin [form="♀ (female)"]
  J22 = female pin header, 2 pins [form="♀ (female)"]
  J25 = female pin header, 20 pins [form="♀ (female)"]  # not connected
  J24 = female pin header, 20 pins [form="♀ (female)"]  # not connected
  J8 = female pin header, 20 pins [form="♀ (female)"]
  J7 = female pin header, 20 pins [form="♀ (female)"]

nets:
  N1: 5V.pin1, MCU1.pin_2, MCU1.pin_4, J7.pin1, J7.pin2
  N2: 5V.pin2, AMP.pin1, AMP.pin3, J5.pin4, I2C2.pin1, C1.1, J13.pin4, J14.pin4, J15.pin4, J16.pin4, MCU1.pin_6, MCU1.pin_9, MCU1.pin_14, MCU1.pin_20, MCU1.pin_25, MCU1.pin_30, MCU1.pin_34, MCU1.pin_39, J6.pin4, I2C.pin1, J23.pin1, U1.-, POW_2.cathode, GND.pin1, -.pin1, SW.pin1, VOUT.pin1, G.pin1, J22.pin1, J8.pin5, J8.pin13, J8.pin20, J7.pin3, J7.pin7, J7.pin10, J7.pin15, J7.pin17
  N3: 5V.pin3, POW.L1, POW.COM, AMP.pin4, J5.pin3, J13.pin3, J14.pin3, J15.pin3, J16.pin3, J6.pin3, J23.pin2, R4.Pin_0, VOUT.pin2, J22.pin2
  N4: POW.L2, VCC.pin1
  N5: AMP.pin2, C1.0, VOL.pin2
  N6: J5.pin1, J5.pin2
  N7: I2C2.pin2, MCU1.pin_5, I2C.pin2, J8.pin3
  N8: I2C2.pin3, MCU1.pin_3, I2C.pin3, J8.pin2
  N9: I2C2.pin4, MCU1.pin_1, MCU1.pin_17, I2C.pin4, R3.Pin_0, 3V.pin1, J8.pin1, J8.pin9
  N10: J13.pin1, J13.pin2
  N11: J14.pin1, J14.pin2
  N12: J15.pin1, J15.pin2
  N13: J16.pin1, J16.pin2
  N14: MCU1.pin_7, J8.pin4
  N15: MCU1.pin_8, J7.pin4
  N16: MCU1.pin_10, J7.pin5
  N17: MCU1.pin_11, J8.pin6
  N18: MCU1.pin_12, J7.pin6
  N19: MCU1.pin_13, J8.pin7
  N20: MCU1.pin_15, J8.pin8
  N21: MCU1.pin_16, J7.pin8
  N22: MCU1.pin_18, J7.pin9
  N23: MCU1.pin_19, J8.pin10
  N24: MCU1.pin_21, J8.pin11
  N25: MCU1.pin_22, J7.pin11
  N26: MCU1.pin_23, J8.pin12
  N27: MCU1.pin_24, J7.pin12
  N28: MCU1.pin_26, J7.pin13
  N29: MCU1.pin_27, J8.pin14
  N30: MCU1.pin_28, J7.pin14
  N31: MCU1.pin_29, J8.pin15
  N32: MCU1.pin_31, J8.pin16
  N33: MCU1.pin_32, J7.pin16
  N34: MCU1.pin_33, VOL.pin1, J8.pin17
  N35: MCU1.pin_35, J8.pin18
  N36: MCU1.pin_36, J7.pin18
  N37: MCU1.pin_37, J8.pin19
  N38: MCU1.pin_38, J7.pin19
  N39: MCU1.pin_40, J7.pin20
  N40: J6.pin1, J6.pin2
  N41: R2.Pin_0, GPIO_LED.pin1
  N42: R2.Pin_1, LED.pin1
  N43: J23.pin3, J23.pin4
  N44: R3.Pin_1, GPIO_SW.pin1, SW.pin2
  N45: SP+.pin1, SP+_2.pin1
  N46: SP-.pin1, SP-_2.pin1
  N47: POW_2.anode, R4.Pin_1
  N48: GPIO_IN.pin1, I.pin1
