# Fritzing sketch OttoPi-06c (saved by Fritzing 0.9.3b)
circuit board: 5.5cm x 6.5cm
perfboards: 1

parts:
  5V = female pin header, 3 pins [form="♀ (female)"]
  P_SW1 = Toggle Switch [package=THT]
  AMP = female pin header, 4 pins [form="♀ (female)"]
  J5 = female pin header, 4 pins [form="♀ (female)"]
  I2C2 = female pin header, 4 pins [form="♀ (female)"]
  C1 = Ceramic Capacitor [capacitance=100nF package="100 mil [THT, multilayer]"]
  J13 = female pin header, 4 pins [form="♀ (female)"]
  MCU1 = Raspberry Pi Zero
  J12 = female pin header, 24 pins [form="♀ (female)"]  # not connected
  VOL = female pin header, 2 pins [form="♀ (female)"]
  J6 = female pin header, 4 pins [form="♀ (female)"]
  R2 = Resistor [tolerance=±5% resistance=330 package=THT]
  J23 = female pin header, 4 pins [form="♀ (female)"]
  R3 = Resistor [tolerance=±5% resistance=10k package=THT]
  U1 = LIPO-2000mAh [package=lipo-2000]
  SP+ = female pin header, 1 pin [form="♀ (female)"]
  SP- = female pin header, 1 pin [form="♀ (female)"]
  SP+_2 = female pin header, 1 pin [form="♀ (female)"]
  SP-_2 = female pin header, 1 pin [form="♀ (female)"]
  POW = LED - 5mm [color="Red (633nm)" package="5 mm [THT]"]
  R4 = Resistor [tolerance=±5% resistance=330 package=THT]
  GND = female pin header, 1 pin [form="♀ (female)"]
  3_7V = female pin header, 1 pin [form="♀ (female)"]
  GPIO_SW = female pin header, 1 pin [form="♀ (female)"]
  GPIO_LED = female pin header, 1 pin [form="♀ (female)"]
  LED = female pin header, 1 pin [form="♀ (female)"]
  G = female pin header, 1 pin [form="♀ (female)"]
  J22 = female pin header, 2 pins [form="♀ (female)"]
  J25 = female pin header, 20 pins [form="♀ (female)"]  # not connected
  J24 = female pin header, 20 pins [form="♀ (female)"]  # not connected
  J8 = female pin header, 20 pins [form="♀ (female)"]
  J7 = female pin header, 20 pins [form="♀ (female)"]
  R = female pin header, 1 pin [form="♀ (female)"]
  L = female pin header, 1 pin [form="♀ (female)"]
  R5 = Resistor [tolerance=±5% resistance=1k package=THT]
  R6 = Resistor [tolerance=±5% resistance=1k package=THT]
  P_SW2 = female pin header, 2 pins [form="♀ (female)"]
  I2C3 = female pin header, 4 pins [form="♀ (female)"]
  SW = female pin header, 1 pin [form="♀ (female)"]
  G_2 = female pin header, 1 pin [form="♀ (female)"]

nets (from the schematic view):
  N1: 5V.pin1, MCU1.pin_2, MCU1.pin_4, J7.pin1, J7.pin2
  GND: 5V.pin2, AMP.pin1, AMP.pin3, J5.pin4, I2C2.pin1, C1.1, J13.pin4, MCU1.pin_6, MCU1.pin_9, MCU1.pin_14, MCU1.pin_20, MCU1.pin_25, MCU1.pin_30, MCU1.pin_34, MCU1.pin_39, J6.pin4, J23.pin4, U1.-, POW.cathode, GND.pin1, G.pin1, J22.pin2, J8.pin5, J8.pin13, J8.pin20, J7.pin3, J7.pin7, J7.pin10, J7.pin15, J7.pin17, I2C3.pin1, G_2.pin1
  N2: 5V.pin3, P_SW1.L1, P_SW1.COM, AMP.pin4, J5.pin3, J13.pin3, J6.pin3, J23.pin3, R4.Pin_0, J22.pin1, P_SW2.pin2
  N3: P_SW1.L2, U1.+, 3_7V.pin1, P_SW2.pin1
  N4: AMP.pin2, C1.0, VOL.pin2
  N5: J5.pin1, J5.pin2
  N6: I2C2.pin2, MCU1.pin_5, J8.pin3, I2C3.pin2
  N7: I2C2.pin3, MCU1.pin_3, J8.pin2, I2C3.pin3
  N8: I2C2.pin4, MCU1.pin_1, MCU1.pin_17, R3.Pin_0, J8.pin1, J8.pin9, I2C3.pin4
  N9: J13.pin1, J13.pin2
  N10: MCU1.pin_7, J8.pin4
  N11: MCU1.pin_8, J7.pin4
  N12: MCU1.pin_10, J7.pin5
  N13: MCU1.pin_11, J8.pin6
  N14: MCU1.pin_12, J7.pin6
  N15: MCU1.pin_13, J8.pin7
  N16: MCU1.pin_15, J8.pin8
  N17: MCU1.pin_16, J7.pin8
  N18: MCU1.pin_18, J7.pin9
  N19: MCU1.pin_19, J8.pin10
  N20: MCU1.pin_21, J8.pin11
  N21: MCU1.pin_22, J7.pin11
  N22: MCU1.pin_23, J8.pin12
  N23: MCU1.pin_24, J7.pin12
  N24: MCU1.pin_26, J7.pin13
  N25: MCU1.pin_27, J8.pin14
  N26: MCU1.pin_28, J7.pin14
  N27: MCU1.pin_29, J8.pin15
  N28: MCU1.pin_31, J8.pin16
  N29: MCU1.pin_32, J7.pin16
  N30: MCU1.pin_33, J8.pin17
  N31: MCU1.pin_35, J8.pin18
  N32: MCU1.pin_36, J7.pin18
  N33: MCU1.pin_37, J8.pin19
  N34: MCU1.pin_38, J7.pin19
  N35: MCU1.pin_40, J7.pin20
  N36: VOL.pin1, R5.Pin_1, R6.Pin_1
  N37: J6.pin1, J6.pin2
  N38: R2.Pin_0, GPIO_LED.pin1
  N39: R2.Pin_1, LED.pin1
  N40: J23.pin1, J23.pin2
  N41: R3.Pin_1, GPIO_SW.pin1, SW.pin1
  N42: SP+.pin1, SP+_2.pin1
  N43: SP-.pin1, SP-_2.pin1
  N44: POW.anode, R4.Pin_1
  N45: R.pin1, R6.Pin_0
  N46: L.pin1, R5.Pin_0
