# Fritzing sketch OttoPi-07a (saved by Fritzing 0.9.3b)
circuit board: 5.5cm x 6.5cm
perfboards: 1

parts:
  DC-DC = female pin header, 3 pins [form="♀ (female)"]
  P_SW = Toggle Switch [package=THT]
  AMP = female pin header, 4 pins [form="♀ (female)"]
  J5 = female pin header, 4 pins [form="♀ (female)"]
  I2C2 = female pin header, 4 pins [form="♀ (female)"]
  C1 = Ceramic Capacitor [capacitance=100nF package="100 mil [THT, multilayer]"]
  J13 = female pin header, 4 pins [form="♀ (female)"]
  MCU1 = Raspberry Pi Zero
  J12 = female pin header, 24 pins [form="♀ (female)"]  # not connected
  VOL = female pin header, 2 pins [form="♀ (female)"]
  J6 = female pin header, 4 pins [form="♀ (female)"]
  J23 = female pin header, 4 pins [form="♀ (female)"]
  U1 = LIPO-2000mAh [package=lipo-2000]
  SP+ = female pin header, 1 pin [form="♀ (female)"]
  SP- = female pin header, 1 pin [form="♀ (female)"]
  SP+_2 = female pin header, 1 pin [form="♀ (female)"]
  SP-_2 = female pin header, 1 pin [form="♀ (female)"]
  LED = LED - 5mm [color="Red (633nm)" package="5 mm [THT]"]
  R4 = Resistor [tolerance=±5% resistance=150 package=THT]
  GND = female pin header, 1 pin [form="♀ (female)"]
  3_7V = female pin header, 1 pin [form="♀ (female)"]
  AUDIO = female pin header, 1 pin [form="♀ (female)"]
  I2C3 = female pin header, 4 pins [form="♀ (female)"]
  5V = female pin header, 1 pin [form="♀ (female)"]
  R7 = Resistor [tolerance=±5% resistance=10k package=THT]
  SW = female pin header, 1 pin [form="♀ (female)"]
  G = female pin header, 1 pin [form="♀ (female)"]
  GPIO_SW = female pin header, 1 pin [form="♀ (female)"]
  LED_2 = female pin header, 1 pin [form="♀ (female)"]
  GPIO_LED = female pin header, 1 pin [form="♀ (female)"]
  R8 = Resistor [tolerance=±5% resistance=150 package=THT]
  G_2 = female pin header, 1 pin [form="♀ (female)"]

nets:
  N1: DC-DC.pin1, MCU1.pin_2, MCU1.pin_4, 5V.pin1
  GND: DC-DC.pin2, AMP.pin1, AMP.pin3, J5.pin4, I2C2.pin1, C1.1, J13.pin4, MCU1.pin_6, J6.pin4, J23.pin1, U1.-, LED.cathode, GND.pin1, I2C3.pin1, G.pin1, G_2.pin1
  N2: DC-DC.pin3, P_SW.L1, P_SW.COM, AMP.pin4, J5.pin3, J13.pin3, J6.pin3, J23.pin2, R4.Pin_0
  N3: P_SW.L2, U1.+, 3_7V.pin1
  N4: AMP.pin2, C1.0, VOL.pin2
  N5: J5.pin1, J5.pin2
  N6: I2C2.pin2, MCU1.pin_5, I2C3.pin2
  N7: I2C2.pin3, MCU1.pin_3, I2C3.pin3
  N8: I2C2.pin4, MCU1.pin_1, I2C3.pin4, R7.Pin_0
  N9: J13.pin1, J13.pin2
  N10: VOL.pin1, AUDIO.pin1
  N11: J6.pin1, J6.pin2
  N12: J23.pin3, J23.pin4
  N13: SP+.pin1, SP+_2.pin1
  N14: SP-.pin1, SP-_2.pin1
  N15: LED.anode, R4.Pin_1
  N16: R7.Pin_1, SW.pin1, GPIO_SW.pin1
  N17: LED_2.pin1, R8.Pin_0
  N18: GPIO_LED.pin1, R8.Pin_1
