# Fritzing sketch OttoPi-01a (saved by Fritzing 0.9.3b)
circuit board: 7.36581cm x 6.51312cm
perfboards: 1

parts:
  MCU1 = Raspberry Pi Zero
  J17 = female pin header, 5 pins [form="♀ (female)"]
  LED1 = LED - 5mm [color="Red (633nm)" package="5 mm [THT]"]
  S1 = Pushbutton [package="[THT]"]
  R1 = Resistor [tolerance=±5% resistance=220 package=THT]
  S2 = Toggle Switch [package=THT]
  J18 = female pin header, 7 pins [form="♀ (female)"]
  J19 = female pin header, 7 pins [form="♀ (female)"]
  J7 = female pin header, 3 pins [form="♀ (female)"]
  J8 = female pin header, 3 pins [form="♀ (female)"]
  J9 = female pin header, 3 pins [form="♀ (female)"]
  J3 = female pin header, 3 pins [form="♀ (female)"]
  J4 = female pin header, 3 pins [form="♀ (female)"]
  J5 = female pin header, 3 pins [form="♀ (female)"]
  J6 = female pin header, 3 pins [form="♀ (female)"]
  R2 = Resistor [tolerance=±5% resistance=220 package=THT]
  VCC1 = Battery
  J24 = female pin header, 5 pins [form="♀ (female)"]
  J25 = female pin header, 2 pins [form="♀ (female)"]
  J26 = female pin header, 2 pins [form="♀ (female)"]
  J27 = female pin header, 11 pins [form="♀ (female)"]
  J16 = female pin header, 5 pins [form="♀ (female)"]

nets:
  N1: MCU1.pin_1, MCU1.pin_17, J17.pin1, J24.pin1, J16.pin1
  N2: MCU1.pin_2, MCU1.pin_4, J19.pin1, J27.pin7
  N3: MCU1.pin_3, J17.pin2, J24.pin2, J16.pin2
  N4: MCU1.pin_5, J17.pin3, J24.pin3, J16.pin3
  N5: MCU1.pin_6, MCU1.pin_9, MCU1.pin_14, MCU1.pin_20, MCU1.pin_25, MCU1.pin_39, J17.pin5, LED1.cathode, S1.Pin_1, S1.Pin_2, J18.pin7, J19.pin7, J7.pin1, J8.pin1, J9.pin1, J3.pin1, J4.pin1, J5.pin1, J6.pin1, VCC1.-, J24.pin5, J27.pin6, J27.pin10, J16.pin5
  N6: MCU1.pin_7, J17.pin4, J24.pin4, J16.pin4
  N7: MCU1.pin_33, J27.pin11
  N8: MCU1.pin_36, R1.Pin_1
  N9: MCU1.pin_37, S1.Pin_3, S1.Pin_4, R2.Pin_0
  N10: MCU1.pin_38, R2.Pin_1
  N11: LED1.anode, R1.Pin_0
  N12: S2.COM, J18.pin1, J7.pin2, J8.pin2, J9.pin2, J3.pin2, J4.pin2, J5.pin2, J6.pin2
  N13: S2.L2, VCC1.+
  N14: J25.pin1, J27.pin2
  N15: J25.pin2, J27.pin1
  N16: J26.pin1, J27.pin3
  N17: J26.pin2, J27.pin4
