# Fritzing sketch RPi0-hat (saved by Fritzing 0.9.3b)
circuit board: 6.45334cm x 2.98165cm

parts:
  MCU1 = Raspberry Pi Zero
  J3 = male pin header, 4 pins [form="♂ (male)"]
  J4 = male pin header, 4 pins [form="♂ (male)"]
  J5 = male pin header, 4 pins [form="♂ (male)"]
  J6 = male pin header, 4 pins [form="♂ (male)"]
  J7 = male pin header, 4 pins [form="♂ (male)"]
  J8 = male pin header, 4 pins [form="♂ (male)"]
  J9 = male pin header, 4 pins [form="♂ (male)"]
  J12 = male pin header, 2 pins [form="♂ (male)"]
  J13 = male pin header, 2 pins [form="♂ (male)"]
  J14 = male pin header, 2 pins [form="♂ (male)"]
  J16 = male pin header, 4 pins [form="♂ (male)"]
  J15 = male pin header, 4 pins [form="♂ (male)"]
  J17 = male pin header, 20 pins [form="♂ (male)"]
  J18 = male pin header, 20 pins [form="♂ (male)"]
  J20 = female pin header, 20 pins [form="♀ (female)"]
  J19 = female pin header, 20 pins [form="♀ (female)"]
  U2 = LIPO-2000mAh [package=lipo-2000]
  M1 = RioRand LM2596  # not connected
  S1 = SPST Switch [package=switch-spdt_lock.007s]  # not connected
  J21 = male pin header, 2 pins [form="♂ (male)"]
  J22 = male pin header, 2 pins [form="♂ (male)"]
  J24 = male pin header, 2 pins [form="♂ (male)"]
  J23 = double row male pin header, 4 pins [form="♂ (male)"]

nets:
  N1: MCU1.pin_1, MCU1.pin_17, J16.pin1, J15.pin1, J18.pin1, J18.pin9, J19.pin1, J19.pin9
  N2: MCU1.pin_2, MCU1.pin_4, J17.pin1, J17.pin2, J20.pin1, J20.pin2
  N3: MCU1.pin_3, J16.pin2, J15.pin2, J18.pin2, J19.pin2
  N4: MCU1.pin_5, J16.pin3, J15.pin3, J18.pin3, J19.pin3
  N5: MCU1.pin_6, MCU1.pin_9, MCU1.pin_14, MCU1.pin_39, J3.pin4, J4.pin4, J5.pin4, J6.pin4, J7.pin4, J8.pin4, J9.pin4, J12.pin2, J13.pin2, J14.pin2, J16.pin4, J15.pin4, J18.pin5, J18.pin20, J19.pin5, J19.pin20, J21.pin2, J22.pin2, J24.pin2
  N6: MCU1.pin_7, J18.pin4, J19.pin4
  N7: MCU1.pin_8, J17.pin4, J20.pin4
  N8: MCU1.pin_10, J17.pin5, J20.pin5
  N9: MCU1.pin_11, J18.pin6, J19.pin6
  N10: MCU1.pin_12, J17.pin6, J20.pin6
  N11: MCU1.pin_13, J18.pin7, J19.pin7
  N12: MCU1.pin_15, J18.pin8, J19.pin8
  N13: MCU1.pin_16, J17.pin8, J20.pin8
  N14: MCU1.pin_18, J17.pin9, J20.pin9
  N15: MCU1.pin_19, J18.pin10, J19.pin10
  N16: MCU1.pin_21, J18.pin11, J19.pin11
  N17: MCU1.pin_22, J17.pin11, J20.pin11
  N18: MCU1.pin_23, J18.pin12, J19.pin12
  N19: MCU1.pin_24, J17.pin12, J20.pin12
  N20: MCU1.pin_26, J17.pin13, J20.pin13
  N21: MCU1.pin_27, J18.pin14, J19.pin14
  N22: MCU1.pin_28, J17.pin14, J20.pin14
  N23: MCU1.pin_29, J18.pin15, J19.pin15
  N24: MCU1.pin_31, J18.pin16, J19.pin16
  N25: MCU1.pin_32, J17.pin16, J20.pin16
  N26: MCU1.pin_33, J18.pin17, J19.pin17
  N27: MCU1.pin_35, J18.pin18, J19.pin18
  N28: MCU1.pin_36, J17.pin18, J20.pin18
  N29: MCU1.pin_37, J18.pin19, J19.pin19
  N30: MCU1.pin_38, J17.pin19, J20.pin19
  N31: MCU1.pin_40, J17.pin20, J20.pin20
  N32: J3.pin1, J3.pin2
  N33: J3.pin3, J4.pin3, J5.pin3, J6.pin3, J7.pin3, J8.pin3, J9.pin3, J12.pin1, J13.pin1, J14.pin1, J24.pin1
  N34: J4.pin1, J4.pin2
  N35: J5.pin1, J5.pin2
  N36: J6.pin1, J6.pin2
  N37: J7.pin1, J7.pin2
  N38: J8.pin1, J8.pin2
  N39: J9.pin1, J9.pin2
  N40: J17.pin3, J20.pin3
  N41: J17.pin7, J20.pin7
  N42: J17.pin10, J20.pin10
  N43: J17.pin15, J20.pin15
  N44: J17.pin17, J20.pin17
  N45: J18.pin13, J19.pin13
  N46: U2.+, J23.pin2
  N47: U2.-, J23.pin4
  N48: J21.pin1, J22.pin1
