# Fritzing sketch OttoPi-universal1 (saved by Fritzing 0.9.3b)
circuit board: 5.83392cm x 3.25093cm
perfboards: 1

parts:
  J1 = female pin header, 3 pins [form="♀ (female)"]
  J2 = female pin header, 3 pins [form="♀ (female)"]
  J3 = female pin header, 3 pins [form="♀ (female)"]
  J4 = female pin header, 3 pins [form="♀ (female)"]
  S1 = Toggle Switch [package=THT]
  J7 = male pin header, 4 pins [form="♂ (male)"]
  J8 = male pin header, 2 pins [form="♂ (male)"]
  J9 = male pin header, 2 pins [form="♂ (male)"]
  C1 = Ceramic Capacitor [capacitance=100nF package="100 mil [THT, multilayer]"]
  J11 = male pin header, 4 pins [form="♂ (male)"]
  J13 = male pin header, 3 pins [form="♂ (male)"]
  J12 = male pin header, 2 pins [form="♂ (male)"]
  J14 = male pin header, 3 pins [form="♂ (male)"]
  J15 = male pin header, 2 pins [form="♂ (male)"]
  J5 = male pin header, 7 pins [form="♂ (male)"]
  J10 = male pin header, 3 pins [form="♂ (male)"]
  J16 = male pin header, 22 pins [form="♂ (male)"]  # not connected
  J17 = male pin header, 12 pins [form="♂ (male)"]  # not connected

nets:
  N1: J1.pin1, J2.pin1, J3.pin1, J4.pin1, J7.pin2, J7.pin4, C1.1, J11.pin4, J12.pin2, J14.pin2, J15.pin2
  N2: J1.pin2, J2.pin2, J3.pin2, J4.pin2, S1.L2, J7.pin1, J14.pin1
  N3: J1.pin3, J5.pin1
  N4: J2.pin3, J5.pin3
  N5: J3.pin3, J5.pin5
  N6: J4.pin3, J5.pin7
  N7: S1.L1, S1.COM, J12.pin1
  N8: J7.pin3, C1.0, J10.pin3
  N9: J8.pin1, J9.pin1
  N10: J8.pin2, J9.pin2
  N11: J11.pin1, J13.pin1
  N12: J11.pin2, J13.pin2
  N13: J11.pin3, J13.pin3
  N14: J14.pin3, J15.pin1
  N15: J10.pin1, J10.pin2
