# Fritzing sketch OttoPi-08a (saved by Fritzing 0.9.3b)
circuit board: 5.49135cm x 6.37312cm
perfboards: 1

parts:
  DC-DC = female pin header, 3 pins [form="♀ (female)"]
  P_SW = Toggle Switch [package=THT]
  AMP = female pin header, 4 pins [form="♀ (female)"]
  J5 = female pin header, 4 pins [form="♀ (female)"]
  C1 = Ceramic Capacitor [capacitance=100nF package="100 mil [THT, multilayer]"]
  J13 = female pin header, 4 pins [form="♀ (female)"]
  MCU1 = Raspberry Pi Zero
  J12 = female pin header, 24 pins [form="♀ (female)"]  # not connected
  VOL = female pin header, 2 pins [form="♀ (female)"]
  J6 = female pin header, 4 pins [form="♀ (female)"]
  J23 = female pin header, 4 pins [form="♀ (female)"]
  U1 = LIPO-2000mAh [package=lipo-2000]
  SP+ = female pin header, 1 pin [form="♀ (female)"]
  SP- = female pin header, 1 pin [form="♀ (female)"]
  SP+_2 = female pin header, 1 pin [form="♀ (female)"]
  SP-_2 = female pin header, 1 pin [form="♀ (female)"]
  G = female pin header, 1 pin [form="♀ (female)"]
  4V = female pin header, 1 pin [form="♀ (female)"]
  AUDIO = female pin header, 1 pin [form="♀ (female)"]
  I2C3 = female pin header, 4 pins [form="♀ (female)"]
  5V = female pin header, 1 pin [form="♀ (female)"]
  G_2 = female pin header, 1 pin [form="♀ (female)"]
  I2C2 = female pin header, 3 pins [form="♀ (female)"]
  G_3 = female pin header, 1 pin [form="♀ (female)"]
  R1 = Resistor [tolerance=±5% resistance=220 package=THT]
  LED = LED - 5mm [color="Red (633nm)" package="5 mm [THT]"]

nets:
  N1: DC-DC.pin1, MCU1.pin_2, 5V.pin1
  GND: DC-DC.pin2, AMP.pin1, AMP.pin3, J5.pin4, C1.1, J13.pin4, MCU1.pin_6, MCU1.pin_14, J6.pin4, J23.pin1, U1.-, G.pin1, I2C3.pin4, G_2.pin1, G_3.pin1, LED.cathode
  N2: DC-DC.pin3, P_SW.COM, AMP.pin4, J5.pin3, J13.pin3, J6.pin3, J23.pin2, R1.Pin_1
  N3: P_SW.L2, U1.+, 4V.pin1
  N4: AMP.pin2, C1.0, VOL.pin2
  N5: J5.pin1, J5.pin2
  N6: J13.pin1, J13.pin2
  N7: MCU1.pin_1, I2C3.pin1, I2C2.pin1
  N8: MCU1.pin_3, I2C3.pin2, I2C2.pin2
  N9: MCU1.pin_5, I2C3.pin3, I2C2.pin3
  N10: VOL.pin1, AUDIO.pin1
  N11: J6.pin1, J6.pin2
  N12: J23.pin3, J23.pin4
  N13: SP+.pin1, SP+_2.pin1
  N14: SP-.pin1, SP-_2.pin1
  N15: R1.Pin_0, LED.anode
